// Logisim project D_flipflop.circ as structural Verilog: 1 circuit, main circuit main
module main (
  input  S,
  output Q,
  output Q_T
);

  wire CLK_out, nand_1_out, nand_2_out, nand_3_out;

  nand nand_1 (nand_1_out, S, S);
  Clock CLK (.out(CLK_out));
  nand nand_2 (nand_2_out, S, CLK_out);
  nand nand_3 (nand_3_out, CLK_out, nand_1_out);
  nand nand_4 (Q, nand_2_out, Q_T);
  nand nand_5 (Q_T, Q, nand_3_out);
endmodule
