// Logisim project Flip_flop.circ as structural Verilog: 1 circuit, main circuit main
module main (
  input  A,
  input  B,
  output QT,
  output Q_T
);

  wire A1_out, A2_out, Clk_out;

  Clock Clk (.out(Clk_out));
  and A1 (A1_out, A, Clk_out);
  and A2 (A2_out, Clk_out, B);
  nor nor_1 (QT, A1_out, Q_T);
  nor nor_2 (Q_T, QT, A2_out);
endmodule
