// Logisim project dfunflop.circ as structural Verilog: 1 circuit, main circuit main
module main (
  input  w,
  input  w_2,
  input  w_3,
  input  w_4,
  input  [1:0] A,
  input  in_6,
  input  in_7,
  input  in_8,
  input  in_9,
  output out_10,
  output out_11,
  output out_12
);

  wire clock_1_out;

  Clock clock_1 (.out(clock_1_out));
  Multiplexer #(.select(2), .enable("false")) multiplexer_1 (
    .in0(w), .in1(w_2), .in2(w_3), .in3(w_4), .out(out_10), .sel(A));
  D_Flip_Flop d_ff_1 (.clk(clock_1_out), .D(in_6), .Q(out_11), .Qn(out_12), .preset(in_9), .en(in_8), .reset(in_7));
endmodule
